# Fritzing sketch Chamber-Wiring (saved by Fritzing 0.9.3b)
breadboards: 1

parts:
  Part3 = Adafruit Pi Cobbler Plus [part_number="Adafruit #2029"]
  Part4 = ADS1115  # not connected
  Part5 = OLED Monochrome 128x32 SPI [part_number=661]  # not connected
  S1 = Pushbutton [package="[THT]"]
  S2 = Pushbutton [package="[THT]"]

nets:
  +3.3V: Part3.SDA, Part3.GPIO24, Part3.+3.3V, Part3.+5V
  N1: Part3.GPIO4, Part3.TXD
  N2: Part3.GPIO17, Part3.GPIO18
  N3: Part3.GPIO27, Part3.GPIO5, Part3.RXD, Part3.GPIO21, Part3.SCL, Part3.GND, Part3.MOSI, Part3.CE1, Part3.GPIO13
  N4: Part3.GPIO22, Part3.GPIO23
  N5: Part3.MISO, Part3.GPIO25
  N6: Part3.EEDAT, Part3.EECLK
  N7: Part3.GPIO6, Part3.GPIO12
  N8: Part3.GPIO19, Part3.GPIO16
  N9: Part3.GPIO26, Part3.GPIO20
  N10: Part3.CE0, Part3.SCLK
  N11: S1.Pin_1, S1.Pin_2
  N12: S1.Pin_3, S1.Pin_4
  N13: S2.Pin_1, S2.Pin_2
  N14: S2.Pin_3, S2.Pin_4

custom parts:
  Adafruit Pi Cobbler Plus: The Raspberry Pi B+/Pi 2/ Pi 3 has landed on the Maker World like a 40-GPIO pinned, quad-USB ported, credit card sized bomb of DIY joy. And while you can use most of our great Model B accessories by hooking up our downgrade cable, its probably a good time to upgrade your set up and accessorize using all of the Model B+'s / Pi 2's / Pi 3's 40 pins. That's why we now carry the Adafruit Assembled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
  ADS1115: ADC ADS1115
  OLED Monochrome 128x32 SPI: These displays are small, only about 1" diagonal, but very readable due to the high contrast of an OLED display. This display is made of 128x32 individual white OLED pixels, each one is turned on or off by the controller chip. Because the display makes its own light, no backlight is required. This reduces the power required to run the OLED and is why the display has such high contrast; we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
